// Logisim project Contador_1.circ as structural Verilog: 1 circuit, main circuit main
module main (
  input  rst,
  input  ena,
  output [3:0] out_3,
  output [3:0] out_4,
  output [3:0] out_5
);

  wire and_1_out, and_2_out, and_3_out, and_4_out, clk_out;

  Clock clk (.out(clk_out));
  Contador contador_1 (
    .ENA(and_1_out), .RST(rst), .CLK(clk_out), .Q1(out_3[3]), .Q2(out_3[2]), .Q3(out_3[1]), .Q4(out_3[0]));
  and and_1 (and_1_out, and_3_out, and_2_out);
  and and_2 (and_2_out, out_4[0], out_4[3]);
  Contador contador_2 (
    .ENA(and_3_out), .RST(rst), .CLK(clk_out), .Q1(out_4[3]), .Q2(out_4[2]), .Q3(out_4[1]), .Q4(out_4[0]));
  and and_3 (and_3_out, ena, and_4_out);
  and and_4 (and_4_out, out_5[0], out_5[3]);
  Contador contador_3 (.ENA(ena), .RST(rst), .CLK(clk_out), .Q1(out_5[3]), .Q2(out_5[2]), .Q3(out_5[1]), .Q4(out_5[0]));
endmodule
