// Logisim project Contador_10bits.circ as structural Verilog: 1 circuit, main circuit Cont_10b
module Cont_10b (
  input  ENA,
  input  RST,
  input  CLK,
  output Q0,
  output Q1,
  output Q2,
  output Q3,
  output Q4,
  output Q5,
  output Q6,
  output Q7,
  output Q8,
  output Q9
);

  wire cont_gen_1_cout, cont_gen_2_cout, cont_gen_3_cout, cont_gen_4_cout, cont_gen_5_cout, cont_gen_6_cout,
       cont_gen_7_cout, cont_gen_8_cout, cont_gen_9_cout;

  Cont_gen cont_gen_1 (.ENA(ENA), .RST(RST), .CLK(CLK), .Cout(cont_gen_1_cout), .Q(Q0));
  Cont_gen cont_gen_2 (.ENA(cont_gen_1_cout), .RST(RST), .CLK(CLK), .Cout(cont_gen_2_cout), .Q(Q1));
  Cont_gen cont_gen_3 (.ENA(cont_gen_2_cout), .RST(RST), .CLK(CLK), .Cout(cont_gen_3_cout), .Q(Q2));
  Cont_gen cont_gen_4 (.ENA(cont_gen_3_cout), .RST(RST), .CLK(CLK), .Cout(cont_gen_4_cout), .Q(Q3));
  Cont_gen cont_gen_5 (.ENA(cont_gen_4_cout), .RST(RST), .CLK(CLK), .Cout(cont_gen_5_cout), .Q(Q4));
  Cont_gen cont_gen_6 (.ENA(cont_gen_5_cout), .RST(RST), .CLK(CLK), .Cout(cont_gen_6_cout), .Q(Q5));
  Cont_gen cont_gen_7 (.ENA(cont_gen_6_cout), .RST(RST), .CLK(CLK), .Cout(cont_gen_7_cout), .Q(Q6));
  Cont_gen cont_gen_8 (.ENA(cont_gen_7_cout), .RST(RST), .CLK(CLK), .Cout(cont_gen_8_cout), .Q(Q7));
  Cont_gen cont_gen_9 (.ENA(cont_gen_8_cout), .RST(RST), .CLK(CLK), .Cout(cont_gen_9_cout), .Q(Q8));
  Cont_gen cont_gen_10 (.ENA(cont_gen_9_cout), .RST(RST), .CLK(CLK), .Q(Q9));  // open: Cout
endmodule
