// Logisim project Contador_generico.circ as structural Verilog: 1 circuit, main circuit Cont_gen
module Cont_gen (
  input  ENA,
  input  RST,
  input  CLK,
  output Cout,
  output Q
);

  wire not_1_out;

  and and_1 (Cout, ENA, Q);
  not not_1 (not_1_out, Q);
  ff_d_ena_rst ff_d_ena_rst_1 (.D(not_1_out), .ENA(ENA), .RST(RST), .CLK(CLK), .SALIDA(Q));
endmodule
