// Logisim project Contador_nbits.circ as structural Verilog: 1 circuit, main circuit main
module main (
  input  in_1,
  input  in_2,
  output out_3,
  output out_4,
  output out_5,
  output out_6
);

  wire clock_1_out, cont_gen_1_cout, cont_gen_2_cout, cont_gen_3_cout;

  Clock clock_1 (.out(clock_1_out));
  Cont_gen cont_gen_1 (.ENA(in_1), .RST(in_2), .CLK(clock_1_out), .Cout(cont_gen_1_cout), .Q(out_4));
  Cont_gen cont_gen_2 (.ENA(cont_gen_1_cout), .RST(in_2), .CLK(clock_1_out), .Cout(cont_gen_2_cout), .Q(out_5));
  Cont_gen cont_gen_3 (.ENA(cont_gen_2_cout), .RST(in_2), .CLK(clock_1_out), .Cout(cont_gen_3_cout), .Q(out_6));
  Cont_gen cont_gen_4 (.ENA(cont_gen_3_cout), .RST(in_2), .CLK(clock_1_out), .Q(out_3));  // open: Cout
endmodule
