// Logisim project Display.circ as structural Verilog: 1 circuit, main circuit main
module main (
  input  in_1,
  input  in_2,
  input  [3:0] in_3,
  input  in_4,
  input  in_5,
  input  in_6
);

  wire and_1_out, and_2_out, CLK, MUX_SAL, rgb_video_1_p1;
  wire [2:0] not_3_out;
  wire [7:0] cont_10b_1_q0, cont_10b_2_q0, rom_1_data;

  Clock clock_1 (.out(CLK));
  ROM #(.addrWidth(7)) rom_1 (.addr({in_3, cont_10b_2_q0[4:2]}), .data(rom_1_data));
  Cont_10b cont_10b_1 (
    .ENA(in_1), .RST(in_2), .CLK(CLK), .Q0(cont_10b_1_q0[0]), .Q1(cont_10b_1_q0[1]), .Q2(cont_10b_1_q0[2]),
    .Q3(cont_10b_1_q0[3]), .Q4(cont_10b_1_q0[4]), .Q5(cont_10b_1_q0[5]), .Q6(cont_10b_1_q0[6]),
    .Q7(cont_10b_1_q0[7]));  // open: Q8, Q9
  and and_1 (and_1_out, cont_10b_1_q0[0], cont_10b_1_q0[1], cont_10b_1_q0[2], cont_10b_1_q0[3], cont_10b_1_q0[4], cont_10b_1_q0[5], cont_10b_1_q0[6], cont_10b_1_q0[7]);
  Multiplexer #(.select(3)) multiplexer_1 (
    .in0(rom_1_data[0]), .in1(rom_1_data[1]), .in2(rom_1_data[2]), .in3(rom_1_data[3]), .in4(rom_1_data[4]),
    .in5(rom_1_data[5]), .in6(rom_1_data[6]), .in7(rom_1_data[7]), .out(MUX_SAL), .sel(not_3_out));
  not not_1 (not_3_out[2], cont_10b_1_q0[4]);
  not not_2 (not_3_out[1], cont_10b_1_q0[3]);
  not not_3 (not_3_out[0], cont_10b_1_q0[2]);
  Cont_10b cont_10b_2 (
    .ENA(and_1_out), .RST(in_2), .CLK(CLK), .Q0(cont_10b_2_q0[0]), .Q1(cont_10b_2_q0[1]),
    .Q2(cont_10b_2_q0[2]), .Q3(cont_10b_2_q0[3]), .Q4(cont_10b_2_q0[4]), .Q5(cont_10b_2_q0[5]),
    .Q6(cont_10b_2_q0[6]), .Q7(cont_10b_2_q0[7]));  // open: Q8, Q9
  and and_2 (and_2_out, cont_10b_2_q0[0], cont_10b_2_q0[1], cont_10b_2_q0[2], cont_10b_2_q0[3], cont_10b_2_q0[4], cont_10b_2_q0[5], cont_10b_2_q0[6], cont_10b_2_q0[7]);
  // RGB_Video #(.height(256), .width(256)) rgb_video_1: pin names not known; wires that end beside it: rgb_video_1_p1, CLK, MUX_SAL, cont_10b_1_q0, cont_10b_2_q0, {in_4, in_6, in_5}
  or or_1 (rgb_video_1_p1, in_2, and_2_out);

  // Other names for the same wires on the sheet: ENA = in_1; RST = in_2

  // Notes on the sheet:
  //   contents of rom_1 (hex, n*v repeats v):
  //   0 3c 66 6e 76 66 3c 0 0 18 38 4*18
endmodule
