// Logisim project Registro.circ as structural Verilog: 1 circuit, main circuit main
module main (
  input  D0,
  input  D1,
  input  D2,
  input  D3,
  input  ena,
  input  rst,
  input  clk,
  output Q0,
  output Q1,
  output Q2,
  output Q3
);

  ff_d_ena_rst ff_d_ena_rst_1 (.D(D0), .ENA(ena), .RST(rst), .CLK(clk), .SALIDA(Q0));
  ff_d_ena_rst ff_d_ena_rst_2 (.D(D1), .ENA(ena), .RST(rst), .CLK(clk), .SALIDA(Q1));
  ff_d_ena_rst ff_d_ena_rst_3 (.D(D2), .ENA(ena), .RST(rst), .CLK(clk), .SALIDA(Q2));
  ff_d_ena_rst ff_d_ena_rst_4 (.D(D3), .ENA(ena), .RST(rst), .CLK(clk), .SALIDA(Q3));
endmodule
