// Logisim project 7_seg.circ as structural Verilog: 4 circuits, main circuit main
module ghghg (
  input  S,
  input  ENA,
  input  CK,
  input  Reset,
  output X4,
  output X3,
  output X2,
  output X1
);

  wire and_1_out, and_2_out, and_3_out, and_4_out, d_ff_1_q, d_ff_2_q, d_ff_3_q;

  and and_1 (and_1_out, X4, ENA);
  D_Flip_Flop d_ff_1 (.D(and_1_out), .clk(CK), .Q(d_ff_1_q), .Qn(X4), .preset(S), .reset(Reset));
  and and_2 (and_2_out, X3, ENA);
  D_Flip_Flop d_ff_2 (.D(and_2_out), .clk(d_ff_1_q), .Q(d_ff_2_q), .Qn(X3), .preset(S), .reset(Reset));
  and and_3 (and_3_out, X2, ENA);
  D_Flip_Flop d_ff_3 (.D(and_3_out), .clk(d_ff_2_q), .Q(d_ff_3_q), .Qn(X2), .preset(S), .reset(Reset));
  and and_4 (and_4_out, X1, ENA);
  D_Flip_Flop d_ff_4 (.D(and_4_out), .clk(d_ff_3_q), .Qn(X1), .preset(S), .reset(Reset));  // open: Q
endmodule

module main (
  input  X1,
  input  X2,
  input  X3,
  input  X4,
  output g,
  output f,
  output a,
  output b,
  output e,
  output d,
  output c
);

  wire and_1_out, and_2_out, and_3_out, and_4_out, and_5_out, and_6_out, and_7_out, and_8_out, and_9_out,
       and_10_out, and_11_out, and_12_out, and_13_out, and_14_out, and_15_out, and_16_out, and_17_out,
       and_18_out, and_19_out;

  and and_1 (and_1_out, X4, X2);
  and and_2 (and_2_out, ~X4, ~X2);  // AND_Gate
  and and_3 (and_3_out, ~X1, ~X2);  // AND_Gate
  and and_4 (and_4_out, ~X3, ~X4);  // AND_Gate
  and and_5 (and_5_out, X3, X4);
  and and_6 (and_6_out, X3, X4);
  and and_7 (and_7_out, ~X1, X2);  // AND_Gate
  and and_8 (and_8_out, ~X2, ~X4);  // AND_Gate
  and and_9 (and_9_out, ~X3, X4, X2);  // AND_Gate
  and and_10 (and_10_out, X3, ~X4);  // AND_Gate
  and and_11 (and_11_out, X3, ~X2);  // AND_Gate
  and and_12 (and_12_out, ~X2, ~X4);  // AND_Gate
  and and_13 (and_13_out, X3, ~X4);  // AND_Gate
  and and_14 (and_14_out, ~X4, ~X3);  // AND_Gate
  and and_15 (and_15_out, ~X3, X2);  // AND_Gate
  and and_16 (and_16_out, ~X4, X2);  // AND_Gate
  and and_17 (and_17_out, X2, ~X3);  // AND_Gate
  and and_18 (and_18_out, X3, ~X4);  // AND_Gate
  and and_19 (and_19_out, X3, ~X2);  // AND_Gate
  or or_1 (a, X1, X3, and_1_out, and_2_out);
  or or_2 (b, X1, and_3_out, and_4_out, and_5_out);
  or or_3 (c, ~X3, and_6_out, and_7_out, X1);  // OR_Gate
  or or_4 (d, X1, and_8_out, and_9_out, and_10_out, and_11_out);
  or or_5 (e, and_12_out, and_13_out);
  or or_6 (f, X1, and_14_out, and_15_out, and_16_out);
  or or_7 (g, X1, and_17_out, and_18_out, and_19_out);
endmodule

module Reloj (
  input  in_1,
  input  in_2,
  input  in_3
);

  wire and_1_out, and_2_out, and_3_out, clock_1_out, ghghg_1_x1, ghghg_1_x2, ghghg_1_x3, ghghg_1_x4,
       ghghg_2_x1, ghghg_2_x2, ghghg_2_x3, ghghg_2_x4, ghghg_3_x1, ghghg_3_x2, ghghg_3_x3, ghghg_3_x4,
       main_1_a, main_1_b, main_1_c, main_1_d, main_1_e, main_1_f, main_1_g, main_2_a, main_2_b, main_2_c,
       main_2_d, main_2_e, main_2_f, main_2_g, main_3_a, main_3_b, main_3_c, main_3_d, main_3_e, main_3_f,
       main_3_g, or_1_out, or_2_out, or_3_out;

  or or_1 (or_1_out, in_1, and_1_out);
  Clock clock_1 (.out(clock_1_out));
  or or_2 (or_2_out, and_3_out, in_1);
  or or_3 (or_3_out, and_2_out, in_1);
  and and_1 (and_1_out, ghghg_1_x1, clock_1_out, ghghg_1_x3);
  and and_2 (and_2_out, ~and_3_out, ghghg_2_x3, ghghg_2_x1);  // AND_Gate
  ghghg ghghg_1 (
    .S(or_1_out), .ENA(in_2), .CK(clock_1_out), .X4(ghghg_1_x4), .X3(ghghg_1_x3), .X2(ghghg_1_x2),
    .X1(ghghg_1_x1));  // open: Reset
  and and_3 (and_3_out, ghghg_3_x3, ~and_1_out, ghghg_3_x2);  // AND_Gate
  ghghg ghghg_2 (
    .S(or_3_out), .ENA(in_3), .CK(and_3_out), .X4(ghghg_2_x4), .X3(ghghg_2_x3), .X2(ghghg_2_x2),
    .X1(ghghg_2_x1));  // open: Reset
  ghghg ghghg_3 (
    .S(or_2_out), .ENA(in_2), .CK(and_1_out), .X4(ghghg_3_x4), .X3(ghghg_3_x3), .X2(ghghg_3_x2),
    .X1(ghghg_3_x1));  // open: Reset
  main main_1 (
    .X1(ghghg_3_x1), .X2(ghghg_3_x2), .X3(ghghg_3_x3), .X4(ghghg_3_x4), .g(main_1_g), .f(main_1_f),
    .a(main_1_a), .b(main_1_b), .e(main_1_e), .d(main_1_d), .c(main_1_c));
  main main_2 (
    .X1(ghghg_1_x1), .X2(ghghg_1_x2), .X3(ghghg_1_x3), .X4(ghghg_1_x4), .g(main_2_g), .f(main_2_f),
    .a(main_2_a), .b(main_2_b), .e(main_2_e), .d(main_2_d), .c(main_2_c));
  main main_3 (
    .X1(ghghg_2_x1), .X2(ghghg_2_x2), .X3(ghghg_2_x3), .X4(ghghg_2_x4), .g(main_3_g), .f(main_3_f),
    .a(main_3_a), .b(main_3_b), .e(main_3_e), .d(main_3_d), .c(main_3_c));
  _7_Segment_Display u_7_segment_display_1 ();  // open: g, f, a, b, e, d, c, dp
  _7_Segment_Display u_7_segment_display_2 (
    .g(main_3_g), .f(main_3_f), .a(main_3_a), .b(main_3_b), .e(main_3_e), .d(main_3_d), .c(main_3_c));  // open: dp
  _7_Segment_Display u_7_segment_display_3 (
    .g(main_1_g), .f(main_1_f), .a(main_1_a), .b(main_1_b), .e(main_1_e), .d(main_1_d), .c(main_1_c));  // open: dp
  _7_Segment_Display u_7_segment_display_4 (
    .g(main_2_g), .f(main_2_f), .a(main_2_a), .b(main_2_b), .e(main_2_e), .d(main_2_d), .c(main_2_c));  // open: dp
endmodule

module prueba_contador (
  input  in_1,
  input  in_2
);

  wire clock_1_out, d_ff_1_q, d_ff_1_qn, d_ff_2_q, d_ff_2_qn, d_ff_3_q, d_ff_3_qn, d_ff_4_qn;

  Clock clock_1 (.out(clock_1_out));
  D_Flip_Flop d_ff_1 (.D(d_ff_1_qn), .clk(clock_1_out), .Q(d_ff_1_q), .Qn(d_ff_1_qn), .preset(in_1), .reset(in_2));
  LED led_1 (.in(d_ff_1_qn));
  D_Flip_Flop d_ff_2 (.D(d_ff_2_qn), .clk(d_ff_1_q), .Q(d_ff_2_q), .Qn(d_ff_2_qn), .preset(in_1), .reset(in_2));
  LED led_2 (.in(d_ff_2_qn));
  D_Flip_Flop d_ff_3 (.D(d_ff_3_qn), .clk(d_ff_2_q), .Q(d_ff_3_q), .Qn(d_ff_3_qn), .preset(in_1), .reset(in_2));
  LED led_3 (.in(d_ff_3_qn));
  D_Flip_Flop d_ff_4 (.D(d_ff_4_qn), .clk(d_ff_3_q), .Qn(d_ff_4_qn), .preset(in_1), .reset(in_2));  // open: Q
  LED led_4 (.in(d_ff_4_qn));
endmodule
