// Logisim project 7segmentos.circ as structural Verilog: 2 circuits, main circuit Siete_seg
module Siete_seg (
  input  X1,
  input  X2,
  input  X3,
  input  X4,
  output g,
  output f,
  output a,
  output b,
  output e,
  output d,
  output c
);

  wire and_1_out, and_2_out, and_3_out, and_4_out, and_5_out, and_6_out, and_7_out, and_8_out, and_9_out,
       and_10_out, and_11_out, and_12_out, and_13_out, and_14_out, and_15_out, and_16_out, and_17_out,
       and_18_out, and_19_out;

  and and_1 (and_1_out, X4, X2);
  and and_2 (and_2_out, ~X4, ~X2);  // AND_Gate
  and and_3 (and_3_out, ~X1, ~X2);  // AND_Gate
  and and_4 (and_4_out, ~X3, ~X4);  // AND_Gate
  and and_5 (and_5_out, X3, X4);
  and and_6 (and_6_out, X3, X4);
  and and_7 (and_7_out, ~X1, X2);  // AND_Gate
  and and_8 (and_8_out, ~X2, ~X4);  // AND_Gate
  and and_9 (and_9_out, ~X3, X4, X2);  // AND_Gate
  and and_10 (and_10_out, X3, ~X4);  // AND_Gate
  and and_11 (and_11_out, X3, ~X2);  // AND_Gate
  and and_12 (and_12_out, ~X2, ~X4);  // AND_Gate
  and and_13 (and_13_out, X3, ~X4);  // AND_Gate
  and and_14 (and_14_out, ~X4, ~X3);  // AND_Gate
  and and_15 (and_15_out, ~X3, X2);  // AND_Gate
  and and_16 (and_16_out, ~X4, X2);  // AND_Gate
  and and_17 (and_17_out, X2, ~X3);  // AND_Gate
  and and_18 (and_18_out, X3, ~X4);  // AND_Gate
  and and_19 (and_19_out, X3, ~X2);  // AND_Gate
  or or_1 (a, X1, X3, and_1_out, and_2_out);
  or or_2 (b, X1, and_3_out, and_4_out, and_5_out);
  or or_3 (c, ~X3, and_6_out, and_7_out, X1);  // OR_Gate
  or or_4 (d, X1, and_8_out, and_9_out, and_10_out, and_11_out);
  or or_5 (e, and_12_out, and_13_out);
  or or_6 (f, X1, and_14_out, and_15_out, and_16_out);
  or or_7 (g, X1, and_17_out, and_18_out, and_19_out);
endmodule

module Siete_seg_hs (
  input  X1,
  input  X2,
  input  X3,
  input  X4,
  output g,
  output f,
  output a,
  output b,
  output e,
  output d,
  output c
);

  wire and_1_out, and_2_out, and_3_out, and_4_out, and_5_out, and_6_out, and_7_out, and_8_out, and_9_out,
       and_10_out, and_11_out, and_12_out, and_13_out, and_14_out, and_15_out, and_16_out, and_17_out,
       and_18_out, and_19_out, and_20_out, and_21_out, and_22_out, and_23_out, and_24_out, and_25_out;

  and and_1 (and_1_out, X1, ~X3);  // AND_Gate
  and and_2 (and_2_out, X3, ~X1);  // AND_Gate
  and and_3 (and_3_out, X4, X2);
  and and_4 (and_4_out, ~X4, ~X2);  // AND_Gate
  and and_5 (and_5_out, ~X1, ~X2);  // AND_Gate
  and and_6 (and_6_out, ~X3, ~X4);  // AND_Gate
  and and_7 (and_7_out, X3, X4);
  and and_8 (and_8_out, X3, X4);
  and and_9 (and_9_out, ~X1, X2);  // AND_Gate
  and and_10 (and_10_out, X1, ~X3);  // AND_Gate
  and and_11 (and_11_out, ~X2, ~X4);  // AND_Gate
  and and_12 (and_12_out, ~X3, X4, X2);  // AND_Gate
  and and_13 (and_13_out, X3, ~X4);  // AND_Gate
  and and_14 (and_14_out, X3, ~X2, ~X1);  // AND_Gate
  and and_15 (and_15_out, ~X2, ~X4);  // AND_Gate
  and and_16 (and_16_out, X3, ~X4);  // AND_Gate
  and and_17 (and_17_out, X1, ~X3);  // AND_Gate
  and and_18 (and_18_out, ~X4, ~X3);  // AND_Gate
  and and_19 (and_19_out, ~X3, X2);  // AND_Gate
  and and_20 (and_20_out, ~X4, X2);  // AND_Gate
  and and_21 (and_21_out, X2, ~X3);  // AND_Gate
  and and_22 (and_22_out, X2, ~X4);  // AND_Gate
  and and_23 (and_23_out, X3, ~X1, ~X2);  // AND_Gate
  and and_24 (and_24_out, X1, ~X4);  // AND_Gate
  and and_25 (and_25_out, X1, ~X3);  // AND_Gate
  or or_1 (a, and_1_out, and_2_out, and_3_out, and_4_out);
  or or_2 (b, X1, and_5_out, and_6_out, and_7_out);
  or or_3 (c, ~X3, and_8_out, and_9_out, X1);  // OR_Gate
  or or_4 (d, and_10_out, and_11_out, and_12_out, and_13_out, and_14_out);
  or or_5 (e, and_15_out, and_16_out);
  or or_6 (f, and_17_out, and_18_out, and_24_out, and_19_out, and_20_out);
  or or_7 (g, and_25_out, and_21_out, and_22_out, and_23_out);
endmodule
