// Logisim project Contador_.circ as structural Verilog: 3 circuits, main circuit Contador
module Contador (
  input  ENA,
  input  RST,
  input  CLK,
  output Q1,
  output Q2,
  output Q3,
  output Q4
);

  wire and_1_out, and_2_out, and_3_out, and_4_out, and_5_out, and_6_out, and_7_out, and_8_out, and_9_out,
       or_1_out, or_2_out, or_3_out, or_4_out;

  and and_1 (and_1_out, ~Q4, ~Q3, Q1);  // AND_Gate
  or or_1 (or_1_out, and_1_out, and_2_out);
  and and_2 (and_2_out, Q2, Q3, Q4);
  ff_d_ena_rst ff_d_ena_rst_1 (.D(or_1_out), .ENA(ENA), .RST(RST), .CLK(CLK), .SALIDA(Q1));
  and and_3 (and_3_out, Q2, ~Q3);  // AND_Gate
  and and_4 (and_4_out, ~Q4, Q2);  // AND_Gate
  or or_2 (or_2_out, and_3_out, and_4_out, and_5_out);
  and and_5 (and_5_out, Q3, Q4, ~Q2);  // AND_Gate
  ff_d_ena_rst ff_d_ena_rst_2 (.D(or_2_out), .ENA(ENA), .RST(RST), .CLK(CLK), .SALIDA(Q2));
  and and_6 (and_6_out, ~Q3, ~Q1, Q4);  // AND_Gate
  and and_7 (and_7_out, Q3, ~Q4);  // AND_Gate
  or or_3 (or_3_out, and_6_out, and_7_out);
  ff_d_ena_rst ff_d_ena_rst_3 (.D(or_3_out), .ENA(ENA), .RST(RST), .CLK(CLK), .SALIDA(Q3));
  and and_8 (and_8_out, ~Q3, ~Q4);  // AND_Gate
  or or_4 (or_4_out, and_8_out, and_9_out);
  and and_9 (and_9_out, Q3, ~Q4);  // AND_Gate
  ff_d_ena_rst ff_d_ena_rst_4 (.D(or_4_out), .ENA(ENA), .RST(RST), .CLK(CLK), .SALIDA(Q4));
endmodule

module Contador_05 (
  input  ENA,
  input  RST,
  input  CLK,
  output Q2,
  output Q3,
  output Q4
);

  wire and_1_out, and_2_out, and_3_out, and_4_out, not_1_out, or_1_out, or_2_out;

  and and_1 (and_1_out, Q4, Q3);
  and and_2 (and_2_out, Q2, ~Q4);  // AND_Gate
  or or_1 (or_1_out, and_1_out, and_2_out);
  ff_d_ena_rst ff_d_ena_rst_1 (.D(or_1_out), .ENA(ENA), .RST(RST), .CLK(CLK), .SALIDA(Q2));
  and and_3 (and_3_out, Q3, ~Q4);  // AND_Gate
  and and_4 (and_4_out, Q4, ~Q2, ~Q3);  // AND_Gate
  or or_2 (or_2_out, and_3_out, and_4_out);
  ff_d_ena_rst ff_d_ena_rst_2 (.D(or_2_out), .ENA(ENA), .RST(RST), .CLK(CLK), .SALIDA(Q3));
  not not_1 (not_1_out, Q4);
  ff_d_ena_rst ff_d_ena_rst_3 (.D(not_1_out), .ENA(ENA), .RST(RST), .CLK(CLK), .SALIDA(Q4));
endmodule

module Contador_011 (
  input  ENA,
  input  RST,
  input  CLK,
  output Q1,
  output Q2,
  output Q3,
  output Q4
);

  wire and_1_out, and_2_out, and_3_out, and_4_out, and_5_out, and_6_out, and_7_out, and_8_out, not_1_out,
       or_1_out, or_2_out, or_3_out;

  and and_1 (and_1_out, ~Q4, Q1);  // AND_Gate
  and and_2 (and_2_out, Q2, Q3, Q4);
  or or_1 (or_1_out, and_1_out, and_3_out, and_2_out);
  and and_3 (and_3_out, ~Q3, Q1);  // AND_Gate
  ff_d_ena_rst ff_d_ena_rst_1 (.D(or_1_out), .ENA(ENA), .RST(RST), .CLK(CLK), .SALIDA(Q1));
  and and_4 (and_4_out, Q2, ~Q3);  // AND_Gate
  and and_5 (and_5_out, ~Q4, Q2);  // AND_Gate
  or or_2 (or_2_out, and_4_out, and_5_out, and_6_out);
  and and_6 (and_6_out, Q3, Q4, ~Q2, ~Q1);  // AND_Gate
  ff_d_ena_rst ff_d_ena_rst_2 (.D(or_2_out), .ENA(ENA), .RST(RST), .CLK(CLK), .SALIDA(Q2));
  and and_7 (and_7_out, ~Q3, Q4);  // AND_Gate
  or or_3 (or_3_out, and_7_out, and_8_out);
  and and_8 (and_8_out, Q3, ~Q4);  // AND_Gate
  ff_d_ena_rst ff_d_ena_rst_3 (.D(or_3_out), .ENA(ENA), .RST(RST), .CLK(CLK), .SALIDA(Q3));
  not not_1 (not_1_out, Q4);
  ff_d_ena_rst ff_d_ena_rst_4 (.D(not_1_out), .ENA(ENA), .RST(RST), .CLK(CLK), .SALIDA(Q4));
endmodule
