// Logisim project Reloj.circ as structural Verilog: 2 circuits, main circuit main
module main (
  input  Config_hs,
  input  Config_min_dec,
  input  Config_min_uni,
  input  Config_seg_dec,
  input  Rst_gral,
  input  in_6
);

  wire and_1_out, and_2_out, and_3_out, and_4_out, and_5_out, and_6_out, clock_1_out, contador_1_q1,
       contador_1_q2, contador_1_q3, contador_1_q4, contador_2_q1, contador_2_q2, contador_2_q3,
       contador_2_q4, contador_05_1_q2, contador_05_1_q3, contador_05_1_q4, contador_05_2_q2,
       contador_05_2_q3, contador_05_2_q4, contador_011_1_q1, contador_011_1_q2, contador_011_1_q3,
       contador_011_1_q4, or_1_out, or_2_out, or_3_out, or_4_out, siete_seg_1_a, siete_seg_1_b,
       siete_seg_1_c, siete_seg_1_d, siete_seg_1_e, siete_seg_1_f, siete_seg_1_g, siete_seg_2_a,
       siete_seg_2_b, siete_seg_2_c, siete_seg_2_d, siete_seg_2_e, siete_seg_2_f, siete_seg_2_g,
       siete_seg_3_a, siete_seg_3_b, siete_seg_3_c, siete_seg_3_d, siete_seg_3_e, siete_seg_3_f,
       siete_seg_3_g, siete_seg_4_a, siete_seg_4_b, siete_seg_4_c, siete_seg_4_d, siete_seg_4_e,
       siete_seg_4_f, siete_seg_4_g, siete_seg_hs_1_a, siete_seg_hs_1_b, siete_seg_hs_1_c, siete_seg_hs_1_d,
       siete_seg_hs_1_e, siete_seg_hs_1_f, siete_seg_hs_1_g, siete_seg_hs_2_a, siete_seg_hs_2_b,
       siete_seg_hs_2_c, siete_seg_hs_2_d, siete_seg_hs_2_e, siete_seg_hs_2_f, siete_seg_hs_2_g;

  and and_1 (and_1_out, contador_011_1_q1, contador_011_1_q3);
  _7_Segment_Display u_7_segment_display_1 (
    .g(siete_seg_hs_1_g), .f(siete_seg_hs_1_f), .a(siete_seg_hs_1_a), .b(siete_seg_hs_1_b),
    .e(siete_seg_hs_1_e), .d(siete_seg_hs_1_d), .c(siete_seg_hs_1_c));  // open: dp
  Siete_seg_hs siete_seg_hs_1 (
    .X4(and_1_out), .g(siete_seg_hs_1_g), .f(siete_seg_hs_1_f), .a(siete_seg_hs_1_a), .b(siete_seg_hs_1_b),
    .e(siete_seg_hs_1_e), .d(siete_seg_hs_1_d), .c(siete_seg_hs_1_c));  // open: X1, X2, X3
  _7_Segment_Display u_7_segment_display_2 (
    .g(siete_seg_hs_2_g), .f(siete_seg_hs_2_f), .a(siete_seg_hs_2_a), .b(siete_seg_hs_2_b),
    .e(siete_seg_hs_2_e), .d(siete_seg_hs_2_d), .c(siete_seg_hs_2_c));  // open: dp
  or or_1 (or_1_out, Config_hs, and_2_out);
  Contador_011 contador_011_1 (
    .ENA(or_1_out), .RST(Rst_gral), .CLK(clock_1_out), .Q1(contador_011_1_q1), .Q2(contador_011_1_q2),
    .Q3(contador_011_1_q3), .Q4(contador_011_1_q4));
  Siete_seg_hs siete_seg_hs_2 (
    .X1(contador_011_1_q1), .X2(contador_011_1_q2), .X3(contador_011_1_q3), .X4(contador_011_1_q4),
    .g(siete_seg_hs_2_g), .f(siete_seg_hs_2_f), .a(siete_seg_hs_2_a), .b(siete_seg_hs_2_b),
    .e(siete_seg_hs_2_e), .d(siete_seg_hs_2_d), .c(siete_seg_hs_2_c));
  and and_2 (and_2_out, and_4_out, and_3_out);
  and and_3 (and_3_out, contador_05_1_q4, contador_05_1_q2);
  or or_2 (or_2_out, Config_min_dec, and_4_out);
  Contador_05 contador_05_1 (
    .ENA(or_2_out), .RST(Rst_gral), .CLK(clock_1_out), .Q2(contador_05_1_q2), .Q3(contador_05_1_q3),
    .Q4(contador_05_1_q4));
  _7_Segment_Display u_7_segment_display_3 (
    .g(siete_seg_1_g), .f(siete_seg_1_f), .a(siete_seg_1_a), .b(siete_seg_1_b), .e(siete_seg_1_e),
    .d(siete_seg_1_d), .c(siete_seg_1_c));  // open: dp
  and and_4 (and_4_out, contador_1_q4, and_5_out, contador_1_q1);
  Siete_seg siete_seg_1 (
    .X2(contador_05_1_q2), .X3(contador_05_1_q3), .X4(contador_05_1_q4), .g(siete_seg_1_g),
    .f(siete_seg_1_f), .a(siete_seg_1_a), .b(siete_seg_1_b), .e(siete_seg_1_e), .d(siete_seg_1_d),
    .c(siete_seg_1_c));  // open: X1
  _7_Segment_Display u_7_segment_display_4 (
    .g(siete_seg_2_g), .f(siete_seg_2_f), .a(siete_seg_2_a), .b(siete_seg_2_b), .e(siete_seg_2_e),
    .d(siete_seg_2_d), .c(siete_seg_2_c));  // open: dp
  or or_3 (or_3_out, Config_min_uni, and_5_out);
  Contador contador_1 (
    .ENA(or_3_out), .RST(Rst_gral), .CLK(clock_1_out), .Q1(contador_1_q1), .Q2(contador_1_q2),
    .Q3(contador_1_q3), .Q4(contador_1_q4));
  Siete_seg siete_seg_2 (
    .X1(contador_1_q1), .X2(contador_1_q2), .X3(contador_1_q3), .X4(contador_1_q4), .g(siete_seg_2_g),
    .f(siete_seg_2_f), .a(siete_seg_2_a), .b(siete_seg_2_b), .e(siete_seg_2_e), .d(siete_seg_2_d),
    .c(siete_seg_2_c));
  and and_5 (and_5_out, contador_05_2_q4, and_6_out, contador_05_2_q2);
  _7_Segment_Display u_7_segment_display_5 (
    .g(siete_seg_3_g), .f(siete_seg_3_f), .a(siete_seg_3_a), .b(siete_seg_3_b), .e(siete_seg_3_e),
    .d(siete_seg_3_d), .c(siete_seg_3_c));  // open: dp
  or or_4 (or_4_out, Config_seg_dec, and_6_out);
  Contador_05 contador_05_2 (
    .ENA(or_4_out), .RST(Rst_gral), .CLK(clock_1_out), .Q2(contador_05_2_q2), .Q3(contador_05_2_q3),
    .Q4(contador_05_2_q4));
  Siete_seg siete_seg_3 (
    .X2(contador_05_2_q2), .X3(contador_05_2_q3), .X4(contador_05_2_q4), .g(siete_seg_3_g),
    .f(siete_seg_3_f), .a(siete_seg_3_a), .b(siete_seg_3_b), .e(siete_seg_3_e), .d(siete_seg_3_d),
    .c(siete_seg_3_c));  // open: X1
  _7_Segment_Display u_7_segment_display_6 (
    .g(siete_seg_4_g), .f(siete_seg_4_f), .a(siete_seg_4_a), .b(siete_seg_4_b), .e(siete_seg_4_e),
    .d(siete_seg_4_d), .c(siete_seg_4_c));  // open: dp
  Clock clock_1 (.out(clock_1_out));
  Contador contador_2 (
    .ENA(in_6), .RST(Rst_gral), .CLK(clock_1_out), .Q1(contador_2_q1), .Q2(contador_2_q2),
    .Q3(contador_2_q3), .Q4(contador_2_q4));
  Siete_seg siete_seg_4 (
    .X1(contador_2_q1), .X2(contador_2_q2), .X3(contador_2_q3), .X4(contador_2_q4), .g(siete_seg_4_g),
    .f(siete_seg_4_f), .a(siete_seg_4_a), .b(siete_seg_4_b), .e(siete_seg_4_e), .d(siete_seg_4_d),
    .c(siete_seg_4_c));
  and and_6 (and_6_out, contador_2_q1, in_6, contador_2_q4);
endmodule

module prueba (
  input  in_1,
  input  in_2
);

  wire and_1_out, clock_1_out, clock_2_out, contador_1_q2, contador_1_q3, contador_1_q4, contador_011_1_q1,
       contador_011_1_q2, contador_011_1_q3, contador_011_1_q4, siete_seg_1_a, siete_seg_1_b, siete_seg_1_c,
       siete_seg_1_d, siete_seg_1_e, siete_seg_1_f, siete_seg_1_g, siete_seg_hs_1_a, siete_seg_hs_1_b,
       siete_seg_hs_1_c, siete_seg_hs_1_d, siete_seg_hs_1_e, siete_seg_hs_1_f, siete_seg_hs_1_g,
       siete_seg_hs_2_a, siete_seg_hs_2_b, siete_seg_hs_2_c, siete_seg_hs_2_d, siete_seg_hs_2_e,
       siete_seg_hs_2_f, siete_seg_hs_2_g;

  _7_Segment_Display u_7_segment_display_1 (
    .g(siete_seg_hs_1_g), .f(siete_seg_hs_1_f), .a(siete_seg_hs_1_a), .b(siete_seg_hs_1_b),
    .e(siete_seg_hs_1_e), .d(siete_seg_hs_1_d), .c(siete_seg_hs_1_c));  // open: dp
  and and_1 (and_1_out, contador_011_1_q1, contador_011_1_q3);
  Siete_seg_hs siete_seg_hs_1 (
    .X4(and_1_out), .g(siete_seg_hs_1_g), .f(siete_seg_hs_1_f), .a(siete_seg_hs_1_a), .b(siete_seg_hs_1_b),
    .e(siete_seg_hs_1_e), .d(siete_seg_hs_1_d), .c(siete_seg_hs_1_c));  // open: X1, X2, X3
  Clock clock_1 (.out(clock_1_out));
  _7_Segment_Display u_7_segment_display_2 (
    .g(siete_seg_hs_2_g), .f(siete_seg_hs_2_f), .a(siete_seg_hs_2_a), .b(siete_seg_hs_2_b),
    .e(siete_seg_hs_2_e), .d(siete_seg_hs_2_d), .c(siete_seg_hs_2_c));  // open: dp
  Contador_011 contador_011_1 (
    .ENA(in_2), .CLK(clock_1_out), .Q1(contador_011_1_q1), .Q2(contador_011_1_q2), .Q3(contador_011_1_q3),
    .Q4(contador_011_1_q4));  // open: RST
  Siete_seg_hs siete_seg_hs_2 (
    .X1(contador_011_1_q1), .X2(contador_011_1_q2), .X3(contador_011_1_q3), .X4(contador_011_1_q4),
    .g(siete_seg_hs_2_g), .f(siete_seg_hs_2_f), .a(siete_seg_hs_2_a), .b(siete_seg_hs_2_b),
    .e(siete_seg_hs_2_e), .d(siete_seg_hs_2_d), .c(siete_seg_hs_2_c));
  _7_Segment_Display u_7_segment_display_3 (
    .g(siete_seg_1_g), .f(siete_seg_1_f), .a(siete_seg_1_a), .b(siete_seg_1_b), .e(siete_seg_1_e),
    .d(siete_seg_1_d), .c(siete_seg_1_c));  // open: dp
  Clock clock_2 (.out(clock_2_out));
  Contador contador_1 (
    .ENA(in_1), .CLK(clock_2_out), .Q2(contador_1_q2), .Q3(contador_1_q3), .Q4(contador_1_q4));  // open: RST, Q1
  Siete_seg siete_seg_1 (
    .X2(contador_1_q2), .X3(contador_1_q3), .X4(contador_1_q4), .g(siete_seg_1_g), .f(siete_seg_1_f),
    .a(siete_seg_1_a), .b(siete_seg_1_b), .e(siete_seg_1_e), .d(siete_seg_1_d), .c(siete_seg_1_c));  // open: X1
endmodule
