// Logisim project Sum_1bit.circ as structural Verilog: 1 circuit, main circuit Sumador_1bit
module Sumador_1bit (
  input  A,
  input  B,
  input  Ci,
  output s,
  output Co
);

  wire and_1_out, and_2_out, and_3_out;

  xor xor_1 (s, Ci, B, A);
  and and_1 (and_1_out, A, B);
  and and_2 (and_2_out, A, Ci);
  and and_3 (and_3_out, B, Ci);
  xor xor_2 (Co, and_1_out, and_2_out, and_3_out);
endmodule
