// Logisim project Sum_4bits.circ as structural Verilog: 1 circuit, main circuit main
module main (
  input  [3:0] in_1,
  input  in_2,
  input  [3:0] in_3,
  output [3:0] out_4,
  output out_5
);

  wire sumador_1bit_1_co, sumador_1bit_2_co, sumador_1bit_3_co;

  Sumador_1bit sumador_1bit_1 (.A(in_1[0]), .B(in_3[0]), .Ci(in_2), .s(out_4[0]), .Co(sumador_1bit_1_co));
  Sumador_1bit sumador_1bit_2 (.A(in_1[1]), .B(in_3[1]), .Ci(sumador_1bit_1_co), .s(out_4[1]), .Co(sumador_1bit_2_co));
  Sumador_1bit sumador_1bit_3 (.A(in_1[2]), .B(in_3[2]), .Ci(sumador_1bit_2_co), .s(out_4[2]), .Co(sumador_1bit_3_co));
  Sumador_1bit sumador_1bit_4 (.A(in_1[3]), .B(in_3[3]), .Ci(sumador_1bit_3_co), .s(out_4[3]), .Co(out_5));
endmodule
