// Logisim project Detector_de_secuencia.circ as structural Verilog: 3 circuits, main circuit main
module main (
  input  E,
  input  Rst,
  output Y
);

  wire and_1_out, clock_1_out, d_ff_1_q, d_ff_2_q;

  Clock clock_1 (.out(clock_1_out));
  and and_1 (and_1_out, d_ff_1_q, ~E);  // AND_Gate
  D_Flip_Flop d_ff_1 (.D(E), .clk(clock_1_out), .Q(d_ff_1_q), .reset(Rst));  // open: Qn, preset
  D_Flip_Flop d_ff_2 (.D(and_1_out), .clk(clock_1_out), .Q(d_ff_2_q), .reset(Rst));  // open: Qn, preset
  and and_2 (Y, E, d_ff_2_q);
endmodule

module fddf (
  input  E,
  input  rst,
  output Y
);

  wire and_1_out, and_2_out, clock_1_out, d_ff_1_q, d_ff_2_q, or_1_out;

  Clock clock_1 (.out(clock_1_out));
  and and_1 (and_1_out, E, d_ff_1_q);
  and and_2 (and_2_out, d_ff_2_q, d_ff_1_q, E);
  or or_1 (or_1_out, and_1_out, and_2_out);
  D_Flip_Flop d_ff_1 (.D(E), .clk(clock_1_out), .Q(d_ff_1_q), .reset(rst));  // open: Qn, preset
  D_Flip_Flop d_ff_2 (.D(or_1_out), .clk(clock_1_out), .Q(d_ff_2_q), .reset(rst));  // open: Qn, preset
  and and_3 (Y, d_ff_1_q, d_ff_2_q);
endmodule

module Tp_final (
  input  E,
  input  rst,
  output salida
);

  wire and_1_out, and_2_out, and_3_out, clk_out, d_ff_1_q, d_ff_2_q, or_1_out, or_2_out;

  Clock clk (.out(clk_out));
  and and_1 (and_1_out, ~E, ~d_ff_1_q, d_ff_2_q);  // AND_Gate
  and and_2 (and_2_out, ~E, ~d_ff_2_q, d_ff_1_q);  // AND_Gate
  and and_3 (and_3_out, ~d_ff_1_q, d_ff_2_q);  // AND_Gate
  or or_1 (or_1_out, E, and_3_out);
  or or_2 (or_2_out, and_1_out, and_2_out);
  D_Flip_Flop d_ff_1 (.D(or_1_out), .clk(clk_out), .Q(d_ff_1_q), .reset(rst));  // open: Qn, preset
  D_Flip_Flop d_ff_2 (.D(or_2_out), .clk(clk_out), .Q(d_ff_2_q), .reset(rst));  // open: Qn, preset
  and and_4 (salida, d_ff_1_q, d_ff_2_q);
endmodule
