// Logisim project Punto2tp.circ as structural Verilog: 1 circuit, main circuit main
module main (
  input  A,
  input  B,
  input  C,
  input  D,
  output SALIDA
);

  wire and_1_out, and_2_out, and_3_out;

  and and_1 (and_1_out, A, ~C);  // AND_Gate
  and and_2 (and_2_out, A, ~B);  // AND_Gate
  and and_3 (and_3_out, B, C, ~D);  // AND_Gate
  or or_1 (SALIDA, and_1_out, and_2_out, and_3_out);
endmodule
